# Fritzing sketch schema (saved by Fritzing 0.9.2b)
breadboards: 1

parts:
  Part1 = Arduino Uno (Rev3)
  LCD1 = LCD screen
  R1 = Photocell (LDR) [package=THT]
  T1 = LM35 Temperature Sensor [package="TO92 [THT]"]
  R2 = Trimmer Potentiometer [maximum_resistance=10kΩ package=THT]
  R3 = Resistor [tolerance=±5% resistance=10k package=THT]

nets (from the breadboard view):
  N1: Part1.A0, T1.Vout
  N2: Part1.A1, R1.pin_0, R3.Pin_1
  N3: Part1.D11_PWM/MOSI, LCD1.E
  N4: Part1.D12/MISO, LCD1.RS
  GND: Part1.GND, LCD1.VSS, LCD1.R/W, LCD1.LED-, T1.GND, R2.leg2, R3.Pin_0
  N5: Part1.D2, LCD1.DB7
  N6: Part1.D3_PWM, LCD1.DB6
  N7: Part1.D4, LCD1.DB5
  N8: Part1.D5_PWM, LCD1.DB4
  N9: LCD1.VDD, LCD1.LED+, R1.pin_1, T1.+Vs, R2.leg1
  N10: LCD1.V0, R2.wiper
